# Fritzing sketch In-Progress (saved by Fritzing 0.7.12b)
breadboards: 1

parts:
  U1 = Arduino Mega
  K1 = Relay [part_number=FRS1B-S package=THT]
  R1 = Resistor [tolerance=±5% resistance=150 package=THT]
  R2 = Resistor [tolerance=±5% resistance=68 package=THT]
  R3 = Resistor [tolerance=±5% resistance=253 package=THT]
  U3 = Voltage Regulator - Variable [package="TO220 [THT]"]
  C2 = Ceramic Capacitor [capacitance=100nF package="100 mil [THT, multilayer]"]
  C3 = Electrolytic Capacitor [capacitance=1µF package="100 mil [THT, electrolytic]"]
  LED1 = LED - 5mm [color="Red (633nm)" package="5 mm [THT]"]
  S1 = Pushbutton [package="[THT]"]
  R4 = Resistor [tolerance=±5% resistance=70k package=THT]

nets:
  N1: U1.+5V, U3.IN, C2.0, S1.Pin_1, S1.Pin_2
  N2: U1.GND, K1.COIL2, R2.Pin_0, R3.Pin_1, C2.1, C3.+, LED1.cathode, R4.Pin_1
  N3: U1.D37, S1.Pin_3, S1.Pin_4, R4.Pin_0
  N4: U1.D46, K1.COIL1
  N5: K1.A, R2.Pin_1
  N6: K1.C1, K1.C2, R1.Pin_0, U3.ADJ
  N7: K1.B, R3.Pin_0
  N8: R1.Pin_1, U3.OUT, C3.-, LED1.anode
